# Fritzing sketch Skematik Lampu Sensor Suara (saved by Fritzing 0.9.5d)

parts:
  Part1 = Arduino Uno (Rev3)
  KY-1 = Keyes Relay [package=THT]
  LED1 = LED - 5mm [color="Red (633nm)" package="5 mm [THT]"]
  Power_plug1 = Power plug
  FC-1 = Sound Sensor

nets:
  N1: Part1.A0, FC-1.OUT
  N2: Part1.D2, KY-1.signal
  5V: Part1.5V, KY-1.power, FC-1.VCC
  GND: Part1.GND, KY-1.ground, FC-1.GND
  N3: KY-1.NC, LED1.cathode
  N4: KY-1.C, Power_plug1.VCC
  N5: LED1.anode, Power_plug1.GND

custom parts:
  Keyes Relay: The Keyes 5V relay module is suitable for SCM development, home appliance control. It uses a 5V~12V TIL control signal which can control DC / AC signal.
